// Logisim project rungpu4d.circ as structural Verilog: 1 circuit, main circuit main
module main (
);

  wire clock_1_out, gpu_lcd_video_256x256x24_1_p5, Reset_out;
  wire [1:0] gpu_lcd_video_256x256x24_1_p3;
  wire [15:0] counter_1_q;
  wire [31:0] rom_1_data;

  Clock clock_1 (.out(clock_1_out));
  Button Reset (.out(Reset_out));
  Counter #(.width(16), .max('h2c8)) counter_1 (
    .count(1'b1), .Q(counter_1_q), .clk(clock_1_out), .clr(Reset_out));  // open: load, D, carry
  ROM #(.addrWidth(16), .dataWidth(32)) rom_1 (.addr(counter_1_q), .data(rom_1_data));  // open: sel
  // GPU_LCD_Video_256x256x24 gpu_lcd_video_256x256x24_1: pin names not known; wires that end beside it: Reset_out, clock_1_out, gpu_lcd_video_256x256x24_1_p3, rom_1_data, gpu_lcd_video_256x256x24_1_p5
  // Probe on gpu_lcd_video_256x256x24_1_p5
  ROM #(.addrWidth(16), .dataWidth(2)) rom_2 (.addr(counter_1_q), .data(gpu_lcd_video_256x256x24_1_p3));  // open: sel

  // Notes on the sheet:
  //   GPU Data In
  //   contents of rom_1 (hex, n*v repeats v):
  //   12000000 1200008a 12000114 1200019e 12000228 120002b2 1200033c 120003c6 12000450 120004da 12000564
  //   120005ee 12000678 12000702 1200078c 12000816 120008a0 1200092a 120009b4 12000a3e 12000ac8 12000b52
  //   12000bdc 12000c66 12000cf0 12000d7a 12000e04 12000e8e 12000f18 12000fa2 1200102c 120010b6 12001140
  //   120011ca 12001254 120012de 12001368 120013f2 1200147c 12001506 12001590 1200161a 120016a4 1200172e
  //   120017b8 12001842 120018cc 12001956 120019e0 12001a6a 12001af4 12001b7e 12001c08 12001c92 12001d1c
  //   12001da6 12001e30 12001eba 12001f44 12001fce 12002058 120020e2 1200216c 120021f6 12002280 1200230a
  //   12002394 1200241e 120024a8 12002532 120025bc 12002646 120026d0 1200275a 120027e4 1200286e 120028f8
  //   12002982 12002a0c 12002a96 12002b20 12002baa 12002c34 12002cbe 12002d48 12002dd2 12002e5c 12002ee6
  //   12002f70 12002ffa 12003084 1200310e 12003198 12003222 120032ac 12003336 120033c0 1200344a 120034d4
  //   1200355e 120035e8 12003672 120036fc 12003786 12003810 1200389a 12003924 120039ae 12003a38 12003ac2
  //   12003b4c 12003bd6 12003c60 12003cea 12003d74 12003dfe 12003e88 12003f12 12003f9c 12004026 120040b0
  //   1200413a 120041c4 1200424e 120042d8 12004362 120043ec 12004476 12004500 1200458a 12004614 1200469e
  //   12004728 120047b2 1200483c 120048c6 12004950 120049da 12004a64 12004aee 12004b78 12004c02 12004c8c
  //   12004d16 12004da0 12004e2a 12004eb4 12004f3e 12004fc8 12005052 120050dc 12005166 120051f0 1200527a
  //   12005304 1200538e 12005418 120054a2 1200552c 120055b6 12005640 120056ca 12005754 120057de 12005868
  //   120058f2 1200597c 12005a06 12005a90 12005b1a 12005ba4 12005c2e 12005cb8 12005d42 12005dcc 12005e56
  //   12005ee0 12005f6a 12005ff4 1200607e 12006108 12006192 1200621c 120062a6 12006330 120063ba 12006444
  //   120064ce 12006558 120065e2 1200666c 120066f6 12006780 1200680a 12006894 1200691e 120069a8 12006a32
  //   12006abc 12006b46 12006bd0 12006c5a 12006ce4 12006d6e 12006df8 12006e82 12006f0c 12006f96 12007020
  //   120070aa 12007134 120071be 12007248 120072d2 1200735c 120073e6 12007470 120074fa 12007584 1200760e
  //   12007698 12007722 120077ac 12007836 120078c0 1200794a 120079d4 12007a5e 12007ae8 12007b72 12007bfc
  //   12007c86 12007d10 12007d9a 12007e24 12007eae 12007f38 12007fc2 1200804c 120080d6 12008160 120081ea
  //   12008274 120082fe 12008388 12008412 1200849c 12008526 120085b0 1200863a 120086c4 1200874e 120087d8
  //   12008862 120088ec 12008976 12008a00 12008a8a 12008b14 12008b9e 12008c28 12008cb2 12008d3c 12008dc6
  //   12008e50 12008eda 12008f64 12008fee 12009078 12009102 1200918c 12009216 120092a0 1200932a 120093b4
  //   1200943e 120094c8 12009552 120095dc 12009666 120096f0 1200977a 12009804 1200988e 12009918 120099a2
  //   12009a2c 12009ab6 12009b40 12009bca 12009c54 12009cde 12009d68 12009df2 12009e7c 12009f06 12009f90
  //   1200a01a 1200a0a4 1200a12e 1200a1b8 1200a242 1200a2cc 1200a356 1200a3e0 1200a46a 1200a4f4 1200a57e
  //   1200a608 1200a692 1200a71c 1200a7a6 1200a830 1200a8ba 1200a944 1200a9ce 1200aa58 1200aae2 1200ab6c
  //   1200abf6 1200ac80 1200ad0a 1200ad94 1200ae1e 1200aea8 1200af32 1200afbc 1200b046 1200b0d0 1200b15a
  //   1200b1e4 1200b26e 1200b2f8 1200b382 1200b40c 1200b496 1200b520 1200b5aa 1200b634 1200b6be 1200b748
  //   1200b7d2 1200b85c 1200b8e6 1200b970 1200b9fa 1200ba84 1200bb0e 1200bb98 1200bc22 1200bcac 1200bd36
  //   1200bdc0 1200be4a 1200bed4 1200bf5e 1200bfe8 1200c072 1200c0fc 1200c186 1200c210 1200c29a 1200c324
  //   1200c3ae 1200c438 1200c4c2 1200c54c 1200c5d6 1200c660 1200c6ea 1200c774 1200c7fe 1200c888 1200c912
  //   1200c99c 1200ca26 1200cab0 1200cb3a 1200cbc4 1200cc4e 1200ccd8 1200cd62 1200cdec 1200ce76 1200cf00
  //   1200cf8a 1200d014 1200d09e 1200d128 1200d1b2 1200d23c 1200d2c6 1200d350 1200d3da 1200d464 1200d4ee
  //   1200d578 1200d602 1200d68c 1200d716 1200d7a0 1200d82a 1200d8b4 1200d93e 1200d9c8 1200da52 1200dadc
  //   1200db66 1200dbf0 1200dc7a 1200dd04 1200dd8e 1200de18 1200dea2 1200df2c 1200dfb6 1200e040 1200e0ca
  //   1200e154 1200e1de 1200e268 1200e2f2 1200e37c 1200e406 1200e490 1200e51a 1200e5a4 1200e62e 1200e6b8
  //   1200e742 1200e7cc 1200e856 1200e8e0 1200e96a 1200e9f4 1200ea7e 1200eb08 1200eb92 1200ec1c 1200eca6
  //   1200ed30 1200edba 1200ee44 1200eece 1200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
  //   GPU Select
  //   contents of rom_2 (hex, n*v repeats v):
  //   702*3
  //   Don't forget to load the GPU's RAM
  //   with the file 'gpu4dram'.
  //   Right click on the GPU video screen.
endmodule
