// Logisim project rungpua.circ as structural Verilog: 1 circuit, main circuit main
module main (
);

  wire clock_1_out, gpu_lcd_video_256x256x24_1_p6, Reset_out;
  wire [1:0] gpu_lcd_video_256x256x24_1_p4;
  wire [15:0] counter_1_q;
  wire [23:0] gpu_lcd_video_256x256x24_1_p3;
  wire [31:0] rom_1_data;

  Clock clock_1 (.out(clock_1_out));
  Button Reset (.out(Reset_out));
  Counter #(.width(16), .max('h3b8)) counter_1 (
    .count(1'b1), .Q(counter_1_q), .clk(clock_1_out), .clr(Reset_out));  // open: load, D, carry
  ROM #(.addrWidth(16), .dataWidth(32)) rom_1 (.addr(counter_1_q), .data(rom_1_data));  // open: sel
  // GPU_LCD_Video_256x256x24 gpu_lcd_video_256x256x24_1: pin names not known; wires that end beside it: Reset_out, clock_1_out, gpu_lcd_video_256x256x24_1_p3, gpu_lcd_video_256x256x24_1_p4, rom_1_data, gpu_lcd_video_256x256x24_1_p6
  // Probe on gpu_lcd_video_256x256x24_1_p6
  ROM #(.addrWidth(16), .dataWidth(2)) rom_2 (.addr(counter_1_q), .data(gpu_lcd_video_256x256x24_1_p4));  // open: sel
  ROM #(.addrWidth(16), .dataWidth(24)) rom_3 (.addr(counter_1_q), .data(gpu_lcd_video_256x256x24_1_p3));  // open: sel

  // Notes on the sheet:
  //   GPU Data In
  //   contents of rom_1 (hex, n*v repeats v):
  //   100ff00 2000000 1ff0000 2001020 100ffff 8002060 8012070 8022080 2000000 1ffff00 50010a0 60040a0
  //   70070a0 9542070 1ffef00 11009070 9682770 1ffdf00 11009170 9692e70 1ffcf00 11009270 9733570 1ffbf00
  //   11009370 9694370 1ffaf00 11009470 9734a70 1ff9f00 11009570 9615870 1ff8f00 11009670 9746670 1ff7f00
  //   11009770 9656d70 1ff6f00 11009870 9737470 1ff5f00 11009970 9747b70 1ffffff 300a1a2 400b4a2 400b4aa
  //   400a1aa 400a1a2 700 f00 f12 712 4 600a09d 14000001 14000203 14000003 14000102 f009000 1000b000
  //   d0040b0 1ff0000 1600c23c 1ffffff 1500c23c 100ff00 1600b23c 1ffffff 1500b23c 10000ff 1600b23c 1ffffff
  //   1500b23c 1ffff00 1600b23c 1ffffff 1500b23c 1ff00ff 1600b23c 1ffffff 1500b23c 100ffff 1600b23c
  //   1ffffff 1500b23c 1ff8f00 1600b23c 1ffffff 1500b23c 10000df 18003808 1ffff00 19000002 17003808
  //   19000102 2003800 19000202 2004f00 19000101 1700b870 19000201 17006274 19000001 1ffffff 20000000
  //   1f000001 8036892 1f000000 80020f4 a000001 a000002 b01ffff b01fdfd b01fbfb b01f9f9 b01f7f7 b01f5f5
  //   b01f3f3 b01f1f1 b01efef b01eded b01ebeb b01e9e9 b01e7e7 b01e5e5 b01e3e3 b01e1e1 b01dfdf b01dddd
  //   b01dbdb b01d9d9 b01d7d7 b01d5d5 b01d3d3 b01d1d1 b01cfcf b01cdcd b01cbcb b01c9c9 b01c7c7 b01c5c5
  //   b01c3c3 b01c1c1 b01bfbf b01bdbd b01bbbb b01b9b9 b01b7b7 b01b5b5 b01b3b3 b01b1b1 b01afaf b01adad
  //   b01abab b01a9a9 b01a7a7 b01a5a5 b01a3a3 b01a1a1 b019f9f b019d9d b019b9b b019999 b019797 b019595
  //   b019393 b019191 b018f8f b018d8d b018b8b b018989 b018787 b018585 b018383 b018181 b017f7f b017d7d
  //   b017b7b b017979 b017777 b017575 b017373 b017171 b016f6f b016d6d b016b6b b016969 b016767 b016565
  //   b016363 b016161 b015f5f b015d5d b015b5b b015959 b015757 b015555 b015353 b015151 b014f4f b014d4d
  //   b014b4b b014949 b014747 b014545 b014343 b014141 b013f3f b013d3d b013b3b b013939 b013737 b013535
  //   b013333 b013131 b012f2f b012d2d b012b2b b012929 b012727 b012525 b012323 b012121 b011f1f b011d1d
  //   b011b1b b011919 b011717 b011515 b011313 b011111 b010f0f b010d0d b010b0b b010909 b010707 b010505
  //   b010303 b010101 b010000 800050b c000003 d03fefe d03fdfd d03fcfc d03fbfb d03fafa d03f9f9 d03f8f8
  //   d03f7f7 d03f6f6 d03f5f5 d03f4f4 d03f3f3 d03f2f2 d03f1f1 d03f0f0 d03efef d03eeee d03eded d03ecec
  //   d03ebeb d03eaea d03e9e9 d03e8e8 d03e7e7 d03e6e6 d03e5e5 d03e4e4 d03e3e3 d03e2e2 d03e1e1 d03e0e0
  //   d03dfdf d03dede d03dddd d03dcdc d03dbdb d03dada d03d9d9 d03d8d8 d03d7d7 d03d6d6 d03d5d5 d03d4d4
  //   d03d3d3 d03d2d2 d03d1d1 d03d0d0 d03cfcf d03cece d03cdcd d03cccc d03cbcb d03caca d03c9c9 d03c8c8
  //   d03c7c7 d03c6c6 d03c5c5 d03c4c4 d03c3c3 d03c2c2 d03c1c1 d03c0c0 d03bfbf d03bebe d03bdbd d03bcbc
  //   d03bbbb d03baba d03b9b9 d03b8b8 d03b7b7 d03b6b6 d03b5b5 d03b4b4 d03b3b3 d03b2b2 d03b1b1 d03b0b0
  //   d03afaf d03aeae d03adad d03acac d03abab d03aaaa d03a9a9 d03a8a8 d03a7a7 d03a6a6 d03a5a5 d03a4a4
  //   d03a3a3 d03a2a2 d03a1a1 d03a0a0 d039f9f d039e9e d039d9d d039c9c d039b9b d039a9a d039999 d039898
  //   d039797 d039696 d039595 d039494 d039393 d039292 d039191 d039090 d038f8f d038e8e d038d8d d038c8c
  //   d038b8b d038a8a d038989 d038888 d038787 d038686 d038585 d038484 d038383 d038282 d038181 d038080
  //   d037f7f d037e7e d037d7d d037c7c d037b7b d037a7a d037979 d037878 d037777 d037676 d037575 d037474
  //   d037373 d037272 d037171 d037070 d036f6f d036e6e d036d6d d036c6c d036b6b d036a6a d036969 d036868
  //   d036767 d036666 d036565 d036464 d036363 d036262 d036161 d036060 d035f5f d035e5e d035d5d d035c5c
  //   d035b5b d035a5a d035959 d035858 d035757 d035656 d035555 d035454 d035353 d035252 d035151 d035050
  //   d034f4f d034e4e d034d4d d034c4c d034b4b d034a4a d034949 d034848 d034747 d034646 d034545 d034444
  //   d034343 d034242 d034141 d034040 d033f3f d033e3e d033d3d d033c3c d033b3b d033a3a d033939 d033838
  //   d033737 d033636 d033535 d033434 d033333 d033232 d033131 d033030 d032f2f d032e2e d032d2d d032c2c
  //   d032b2b d032a2a d032929 d032828 d032727 d032626 d032525 d032424 d032323 d032222 d032121 d032020
  //   d031f1f d031e1e d031d1d d031c1c d031b1b d031a1a d031919 d031818 d031717 d031616 d031515 d031414
  //   d031313 d031212 d031111 d031010 d030f0f d030e0e d030d0d d030c0c d030b0b d030a0a d030909 d030808
  //   d030707 d030606 d030505 d030404 d030303 7*d030202 d0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
  //   GPU Select
  //   contents of rom_2 (hex, n*v repeats v):
  //   50*3 5*2 849*3
  //   GPU Address
  //   contents of rom_3 (hex, n*v repeats v):
  //   0 4*800000 800001 800001 800001 800010 800010 40*82002d ff001 ff002 ff003 ff004 ff000 ff000 4*835828
  //   820032 820032 820033 820033 4*83582c 4*83582e 4*835830 4*835832 4*835834 4*835836 835838 835838
  //   835838 6*83583a 4*800000 5*83583a 83583b 83584f 83584c 83584c 800011 80002b 130*825827 800011
  //   262*835853 136*820032 820f70 130*820033 132*81002c
endmodule
