// Logisim project rungpuhc3.circ as structural Verilog: 1 circuit, main circuit main
module main (
);

  wire clock_1_out, gpu_lcd_video_256x256x24_1_p5, Reset_out;
  wire [1:0] gpu_lcd_video_256x256x24_1_p3;
  wire [15:0] counter_1_q;
  wire [31:0] rom_1_data;

  Clock clock_1 (.out(clock_1_out));
  Button Reset (.out(Reset_out));
  Counter #(.max('h3b8), .width(16)) counter_1 (
    .count(1'b1), .Q(counter_1_q), .up(1'b1), .clk(clock_1_out), .clr(Reset_out));  // open: load, D, carry
  ROM #(.addrWidth(16), .dataWidth(32)) rom_1 (.addr(counter_1_q), .data(rom_1_data));
  // GPU_LCD_Video_256x256x24 gpu_lcd_video_256x256x24_1: pin names not known; wires that end beside it: Reset_out, clock_1_out, gpu_lcd_video_256x256x24_1_p3, rom_1_data, gpu_lcd_video_256x256x24_1_p5
  // Probe on gpu_lcd_video_256x256x24_1_p5
  ROM #(.addrWidth(16), .dataWidth(2)) rom_2 (.addr(counter_1_q), .data(gpu_lcd_video_256x256x24_1_p3));

  // Notes on the sheet:
  //   contents of rom_1 (hex, n*v repeats v):
  //   compressed eJx9mV3So7gSRN+9Cj/fJ1UhQCyHP+9/CZN5KHvmzkQ0RPT5bEiXASlL6Y7WPp/W3qN5e2d7GH7z
  //   eR0t9dqnfT7PaWFkW9prtMi2Wp3ZxvMp8X+f8ny43sjrPfvg3t5La118rU1avd7mzqfo9Nunh6pt
  //   fmNbRq7Pget3IDiw5b22lw6cvwPpA+s0zY/i+B2YHkWfngP770DXR0jR9+fA9jswo4h5PAfG78BC
  //   jb4sz4FVB14cWFHMy/UcWH6K8XyrtT8H5t+B7fmo9Xiug9s7tbbHnu/e2tF/3E29/2W+fVfjrfv3
  //   8l96rQ/1X9P7E8/R/l7rr/buL93xvW3Xe0zzyPGO3p7nyB8pWb1Tf+iR88wmPnlrvkj9c7R6ltP0
  //   vvwMj78HCp98vkOVzpzO9/eKYn7eeMV3oPnEmxOPf5/4vOHP81DTiVP7nfj674nf0eUT80+f6NM+
  //   nxcn9j+Xfka5T1z+c+Lrn584fqXHHz6RE/bnmi59gCbINNr4fffYuO/69uv3yPZ9AL8ZqffrzGz5
  //   +vv9/vuE8JysUvqgg3H7CIJ3llz7t1j8biWS4ztdn8vp+vafGh681kW0aRlbft9vfIUoF/h0vmke
  //   7/2rSj3htV7m+2iUg9fnepnH5+D19tng+lnh/Jnh9JmgdvOWL8DrRn8fN/p7u9Hf643+nm/093Sj
  //   v7WbKov+0mb9dVzor+1Cf60X+mu+0F/Thf7Sbp5yGXid6M/jRH9uJ/pzPdGf84n+nE70p3ZTl4te
  //   ZdEf2ni9HegPmQCcD/THdKA/tJu7PAteO/r92NHv245+X3f0+7yj36cdvbwCvW4zel0uepVFv2mD
  //   64Z+mzf027Sh37SbQ6MdXgP9OAb6sQ30Yx3oxzzQa06gH9pNPV70us3odbnoVRb9qg3OK3rZJfpV
  //   u7nIT+G1oF+OBf0iV4frgl7+i36ZFvSLdlPDCr0eL3rdZvS6XPQqi37WBqcZ/azd7J+Ovl8dfT86
  //   +r519F02DueOvk8dfdduajij17BCr8eLXrcZvS4Xvcqin7RB7WZ+En1eiT6PRJ9bos810eec6HNK
  //   9Knd9ESCGtDWe2DxWg8Y6kZDXTBUYajNbJ+Gvl0NvYwfvVoDevVq9G1u6NvU0ONLZqsVRgTeMUtu
  //   b9FdPqvvXG3SJL+hpivUtIN2C1PT4GXaNUwNS2j3MDVMoF3E1GODdhNTtxG9XcXUZZm4i6kNymXg
  //   eVMftzH3m/q4jjlu6uM+5nJTHxcy+0193MjMm/q4ktlu6uNOpgpDbVB2A+1Wpqa/9biWqekI7V6m
  //   pge0i5kartBuZmr4oLermXqcJu5m6oKhCkNt0G5n7if1cT1znNTH/czlpD4uaPaT+rihmSf1cUWz
  //   ndTHHU3daKgLhioM7ZambM96XNOUDUG7pylbgHZRU9MU2k1NTRv0dlXT6xcRdzX1gKFuNNQFQ7ut
  //   qc16XNccO/VxX3PZqY8Lm32nPm5s5k59XNn02lfEnU0NLKgHDHWjod3aVGHrcW1T9gvt3qbsENrF
  //   TdkTtJubsgv0dnVT09fE3U0NaKiBBfWAod3e1AVbj+ub2qDd31wG9ekCZh/UpxuYOahPV7hY7VCf
  //   7mBqIkENaKiBBd0tTN1o6+kapgpDdw9TbQC6i5iyZehuYsom0burmI4YIt3F1ASGmkhQAxq625h6
  //   wNbTdUxdMHT3MbVBdyGzL9SnG5m5UJ+uZCpBmXQnU8YBNYGhJhJ0tzI1sKyna5m60dDdy1Rh6C5m
  //   qh1BdzNT7QG9u5opHzbpbqYMC8o4oCYwdLczNaCtp+uZesDQ3c/UBUN3QVMbdDc0s1OfrmgqQZh0
  //   R1NGCWVYUMYB3S1NTSTr6Zqml96mu6epGw3dRU0VhhN5ZVJTpD5d1VSbMumupgwayiihDAu625qa
  //   wNbTdU1HKdPd19QDhu7Cpi4Yuhub2tC7K5sO1iLd2VRjgDJoKKOE7tamjMN6urapiQTdvU0NLOgu
  //   bupGQ3dzU4XRu6ubjuoi3d1UQ4JqDFAGDd3tTRmW9XR903HFdPc3NaChVwGmHjD0amD9n/9yfhGf
  //   jHSuunCV/mfSfH5qUEX/cTm+aAXx7yOvOCuw+NWXSdZIqh78PLFAf0tT3x7qql6mr1bkLpjaoe+a
  //   6btp+i6buvtQT8V6ntbh3z0SvTfop256NJgeJaZGD9Sosp7RJjIKTe3Qo9b0aDY9yk2NfqhZYT2z
  //   RWQWmdqhZ53p2Wh6lpqavVCz2npmu4gLmNqhXcO0m5h2GVPuA+VK1uNWIi5maod2PdNuaNolTbkn
  //   lKtaj9uKuLCpHdq1Tbu5aZc35f5QXcF6uoVIFzG1Q3cd093IdJcy1b2gupr1dDuRLmhqh+6aprup
  //   6S5rqvtCdWXr6dYiXdzUDt31Ta8GTK8STG1QqwrrWW2IrEJM7dCrFtOrGdOrHFPLEKhVkfWslkRW
  //   UaZ26FWX6dWY6VWaqcJQm/Ws9kRWgaZ26FWj6dWk6VWmqWUR1PLQelarIqtYUzv0qtf0atj0KtnU
  //   BUMVtp7Vtsgq3NQOvWo3vZo3vco3tUyDWq5aT1rAIv5pBPKSj8bTWb891I9V5/fnrptfM+1BiQdd
  //   jZ983n79pI7wX7x+Uke0DrNSR7Tls6F/Uke0AbNSR7QdZqWOaCfMSh3R7k9YX6kj/IaPV+qISJiV
  //   OiI6zEodEctN/UodEQNmpY6IHWaljogTZqWOiPumfqWOyAazUkdkwqzUEdlhVuqIXC7qV+qIHDAr
  //   dUTuMCt1RJ4wK3X48qhfqSPUZqhfqSPUdqlfqSO0DKF+pY7Qsoz6lTpCy1TqV+oILdupX6kjFGOo
  //   X6kjFOuoX6kjeoNZqSN6wqzUEb3DrNQRfTmoX6kj+oBZqSP6DrNSR+jrU79Shx8n9St1xNxgVuqI
  //   OWFW6oi5w6zUEfOyU79SR8wDZqWOmHeYlTpiPmFW6oj53qlfqSOWBrNSRywJs1JHLB1mpY5Ylo36
  //   lTpiGTArdYS+HvUrdYQeF/UrdXj4Ur9SR6wNZqWOWBNmpY5YO8xKHbGqIPondcQ6YFbqiHWHWakj
  //   1hNmpY5Y7xGvoWmvxd1RywgdrhASo8GsEBIjYVYIidHXw+UrhMRYYFYICX0bvk6FkNDT4etUCAmN
  //   1gn9E0I8e82sEBJbg1khJLaEWSEkNo0/6yuExLbArBAS24BZISS2HWaFkNjOhfoVQmK7YVYIib3B
  //   rBASe8KsEBJ7n6lfIST08dSvEBK6+9SvEBIajdSvEBKandSvEGK3on6FkDgazAohcSTMCiFxaD5a
  //   XyEkjgVmhZA4BswKIXHsMCuExHF26lcIieOGWSFEK0uYFULiTJgVQkJy6lcICd1O6lcICY026lcI
  //   Cc0+6lcICbkR9SuE2J2pXyHEDY36FULiSpgVQuKSP1lfISSuBWaFkLgGzAohce0wK4TEpQtC/4SQ
  //   uG6YFULcIalfISR0mPoVQkK3i/oVQkLDh/oVQkKzi/oVQkJuQ/0KISH3pX6FEHcj6lcI8X8xUL9C
  //   SHwSZoWQ+Mivra8QEp8FZoWQ+AyYFULis8MkhPi1HjB6Bwu/1gW/758PPP9Vcdf/k/wFsOoTtg==
  //   GPU Data In
  //   contents of rom_2 (hex, n*v repeats v):
  //   3 1 4*3 1 3 3 3 1 3 3 1 40*3 1 2 1 2 1 2 1 2 1 2 3 1 4*3 1 3 3 1 3 3 1 4*3 1 4*3 1 4*3 1 4*3 1 4*3 1
  //   4*3 1 3 3 3 1 6*3 1 3 3 1 3 3 1 5*3 1 3 1 3 1 3 3 1 3 1 3 1 130*3 1 3 1 262*3 1 136*3 1 3 1 130*3 1
  //   132*3
  //   GPU Select
endmodule
