// Logisim project rungpuhc3a.circ as structural Verilog: 1 circuit, main circuit main
module main (
);

  wire clock_1_out, gpu_lcd_video_256x256x24_1_p6, Reset_out;
  wire [1:0] gpu_lcd_video_256x256x24_1_p4;
  wire [15:0] counter_1_q;
  wire [23:0] gpu_lcd_video_256x256x24_1_p3;
  wire [31:0] rom_1_data;

  Clock clock_1 (.out(clock_1_out));
  Button Reset (.out(Reset_out));
  Counter #(.max('h3b8), .width(16)) counter_1 (
    .count(1'b1), .Q(counter_1_q), .up(1'b1), .clk(clock_1_out), .clr(Reset_out));  // open: load, D, carry
  ROM #(.addrWidth(16), .dataWidth(32)) rom_1 (.addr(counter_1_q), .data(rom_1_data));
  // GPU_LCD_Video_256x256x24 gpu_lcd_video_256x256x24_1: pin names not known; wires that end beside it: Reset_out, clock_1_out, gpu_lcd_video_256x256x24_1_p3, gpu_lcd_video_256x256x24_1_p4, rom_1_data, gpu_lcd_video_256x256x24_1_p6
  // Probe on gpu_lcd_video_256x256x24_1_p6
  ROM #(.addrWidth(16), .dataWidth(2)) rom_2 (.addr(counter_1_q), .data(gpu_lcd_video_256x256x24_1_p4));
  ROM #(.addrWidth(16), .dataWidth(24)) rom_3 (.addr(counter_1_q), .data(gpu_lcd_video_256x256x24_1_p3));

  // Notes on the sheet:
  //   contents of rom_1 (hex, n*v repeats v):
  //   compressed eJyFmUuW4zgSBPc6Ra5nRYTA33H40/2PMG4mVE6/XtRQr9syRLlCBIEIOKtN0+czTT81efw0om/c
  //   pkrM+c/nZ5sSLVPYalph1bRNr3/o/J4Z3TH9LNPU4Trl0+E+d3X53MPnWr54zxuvfdlq/Z64f0+0
  //   vLEvez3fE9fvieLE+n7P3xNnTrw88f4q+vt74vhV9K+iH98T+++JWUWbt/yInNh+Tywq+rJ8Fevv
  //   iVXFvNzfE8vvCb4iOdb+PTH/nti/X7We6xihjOR7mo521E+fprP/8nh13z9++jifkfvhiz4tf+e/
  //   zpge036/WnfM249/1PT+Ge+MP3LjUO7el/zv5I+bG3L+3uBXy7dd9b5+f1eb/7wxpgSfOP/9iXN8
  //   gs+8/vKJMR3++on/9x1j6v31O7bPuJa//NI7b2T+vrdp+98P2x2x+slU88zLdxi68o3xkfq+0X81
  //   jXGP5tzW349831lq7a/xve33p4wFwsCPM9v0Xra9/rwxfdfWp/8c3w+8jvHTzskvkffnlufnlPtn
  //   l+tnlfNnlu/P+wXzIn6y2uT9qH/OR/2zP+qf9VH/zI/65/2of/IiTlr1dw553urv/VZ/r7f6e77V
  //   3+9b/Z0X8ZW1K+9L/XVe6q/9Un+tl/prvtRf70v9lRdxLld90qo/c8j9VH9macn5VH++T/VnXsRH
  //   KoG8D/XHeag/9kP9sR7qj/lQf7wP9VmB6jPM6nO56pNW/Z5Drrv6fd7V7+9d/Z4X8ZYJKu9N/XZu
  //   6rd9U7+tm/pt3tRv7039lhdxbq/6DLP6XK76pFW/5pDzqj5FSP2aF/GSKiXvRf1yLuqX1Eq5LupT
  //   1dQv70X9khdxppX63F71GWb1uVz1Sat+ziHfs/o5L+L+6er73dX3s6vve1ffUxzl3NX3d1ff8yLO
  //   dFafaaU+t1d9hll9Lld90qp/50D/zou4PqW+7lJfZ6mvvdTXWuprLvX1LvWVFzELSWZCy0wsmRss
  //   M9AyFyyTGD0H8fSZ1E/3pD4VWH2Ks/p0QPXTPKmf3pN6ywwc9SHnz59rFPl7emdZP5K6ALPQZBbM
  //   C2biG1MnYCaipF7ATAxJ3YC5UZL6ATNwxtQRmAuB1hOYQ1JX4PWYn/qC/jke81tn4PaY33oDl8f8
  //   1h3YH/Nbf2A95rcOwekxv/UIJrGkLsEUGJlCgT7L3fzWKZgFKKlXMAtCUrdgJqikfsFMGGPqGMwN
  //   hNYzmAuW1DWYQ6a+ob+Oy/zWObhd5rfeweUyv3UP9sv81j9Yl/mtg3C6zG89hBloSV2ESSxzoE+Z
  //   M791EqbwSOolTCGQ1E2YhSmpnzALxZg6Ctk6hNZTmBssqaswFyyTGP2Rw5g6C7fD/NZbuBzmt+7C
  //   fpjf+gvrML91GLKHDK3HMBNLUpdhBlrmgtEnrfmt0zAFV1KvYQqgpG7DFCRJ/YYpEMbUcZgFC63n
  //   MBNaUtdhbrDMQKPP5ZrfOg9zSOo9XDbzW/dh38xv/Ye1md8+cLtBMb/9AGYhSfoCzMSSucHoM8zm
  //   t0/AJJb0C5jCL+kbMIVY0j9gCqMxfQSydw/tJzALWNJXYCa0zMRCn9trfvsMzAVL+g3MIek7sC/m
  //   t//AWsxvH4J4j9B+BFM4JH0JZiHJTGj0mVbmt0/BDLSkX8EklvQtmAYk6V8wDcGYPgZTgKH9DKZg
  //   SfoazAKWWUjoM53Nb5+DucGSfgdzwZK+B3NI+h+sbn77IMzmHdoPYQqlpC/CFA6ZBYyehWRMn4SZ
  //   WJJ+CTPQkr4Jk1jSP2EaoTF9FKYxQfspTIGW9FWYgiVTONBn+ZrfPgszoSX9FuYGS/ouzAVL+i/M
  //   YUwfhnjR0H4M0xgkfRmmUMoULPRs4Izp0zALSdKvYSaWpG/DDLSkf8MkNqaPw7RiaD+HaUiSvg5T
  //   oGUKJfqUK/Pb5yHeA9LvYSa0pO/D3GBJ/1//w184j/DrZ641F57U2rr6Y+v448Z/ZLPw7zOvdg17
  //   QfSHpa0o0506+kXy8yA/G+ZyXpDLDL18yLBAhgsyjJDhhQw7zO1A7206eVRQ6r2tkNsNmQaQ6QGZ
  //   NjDTCb3TLHT6QaYlZLpCpjFkekOmPcxyQO8yCV0+kGUFWW6QZQhZnpBlC7Oc0bvMQ5c/pCxAygWk
  //   jEDKC6TswJQj9Jap0PIFKWuQcgcpg5DyCCmbMOUUvWU2tPxCyjKkXEPKOKS8Q8o+TDtAb5sIbR+Q
  //   tgJpN5A2BGlPkLYF087Q2+ZC2x+kLULaJaSNQtorpO3CtGP0tunQ9g1p65B2D9kGQLYHkG0DzHYC
  //   vduM0O0HZFsC2a5AtjGQ7Q1k2wOzHULvNil0+wTZVkG2W5BtGGR7Btm2wRzo3eaFbv8g20LIdhGy
  //   jYRsLyHbTph9IXq3qaHbV8i2FrLdhWyDIdtjyLYZJjF6t9mh22/IthyyXYds4yHbe8i2H2afil6b
  //   YIn4ZyG4xvOF68+jisdnfZSbstzck89eXsRfg9H4y/M8gCDusobBaNMiaxiMNm2fVf3XYLTpkIXB
  //   ML5kDYPRpkfWMBiNN9APg9FayfIBBnGXNQxGa4usYTBa2x7zD4PR2iELg2F8yRoGo7VH1jAYrabb
  //   /MNgtCpZPgAh7rKGwWi1yBoGo9V2m38YjFaHLAyG8SVrGAwuz/zDYLR0FPMPg9HSYc3vAxTiLmsY
  //   jJYdmPmHwWjZkZp/GIyWHbr5MRjGl6xhMFocnPmHwWh9Os0/DEbrJcsHMMRd1jAYrS+yhsFofTvN
  //   PwxG64csDIbxJWsYDG6n+YfBaHMmDPphMNpcsnyAQ9xlDYPR5kXWMBht3g7zD4PR5kMWBsP4kjUM
  //   RpsfWcNgtGXazT8MRltKlg+AiLusYTDassgaBqMt227+YTBafp75MRjGl6xhMJi+5h8Go61ZQOiH
  //   wWhryfIBEnGXNQxGWxdZw2C0ddvMPwxGWw9ZGAzjS9YwGG19fOD03THkfYxG9G2bNBw1jEbbSpYP
  //   ooi7rGE02rbIwmio3zQcNYxGy23xd2A0jC9Zw2iwbB0HjAb6fdJw1DAabS9ZPsgi7rKG0Wj7Iguj
  //   oX7TcNQwGm0/ZGE0jC9Zw2i0/ZGF0UB/TBqOGkajHSXLB2HEXdYwGi1fb36MhvpNw1HDaLRMQ/Nj
  //   NIwvWcNoUKbMj9FAf04ajhpGo50lywdpxF3WMBrtXGRhNNRvGo4aRqOdhyyMhvElaxiNdj6yMBro
  //   r0nDUcNotKtk+SCOuMsaRqNlOM2P0VC/aThqGI2WZWd+jIbxJWsYDcqy+Wl16GkRxl+j0e6S5YM8
  //   4i5rGI12L7LYKqnfNBw1jEa7D1lsJY0vWcNotPuRhdFAn9Zo/mE0Wk6b3weBxF3WMBot08f8GA31
  //   m4ajhtFoKTPmx2gYX7KG0aANmR+jgZ5/JDH+Go32KVk+SCTusobRaJ9F8m9t5v9sGo4aRqN9DlkY
  //   DeNLfj0EcS745/nWAfXsB57xDxP/Bbll4m0=
  //   GPU Data In
  //   contents of rom_2 (hex, n*v repeats v):
  //   50*3 5*2 849*3
  //   GPU Select
  //   contents of rom_3 (hex, n*v repeats v):
  //   0 4*800000 800001 800001 800001 800010 800010 40*82002d ff001 ff002 ff003 ff004 ff000 ff000 4*835828
  //   820032 820032 820033 820033 4*83582c 4*83582e 4*835830 4*835832 4*835834 4*835836 835838 835838
  //   835838 6*83583a 4*800000 5*83583a 83583b 83584f 83584c 83584c 800011 80002b 130*825827 800011
  //   262*835853 136*820032 820f70 130*820033 132*81002c
  //   GPU Address
endmodule
