// Logisim project rungpuhc4d2.circ as structural Verilog: 1 circuit, main circuit main
module main (
);

  wire clock_1_out, gpu_lcd_video_256x256x24_1_p5, Reset_out;
  wire [1:0] gpu_lcd_video_256x256x24_1_p3;
  wire [15:0] counter_1_q;
  wire [31:0] rom_1_data;

  Clock clock_1 (.out(clock_1_out));
  Button Reset (.out(Reset_out));
  Counter #(.max('h2c8), .width(16)) counter_1 (
    .count(1'b1), .Q(counter_1_q), .up(1'b1), .clk(clock_1_out), .clr(Reset_out));  // open: load, D, carry
  ROM #(.addrWidth(16), .dataWidth(32)) rom_1 (.addr(counter_1_q), .data(rom_1_data));
  // GPU_LCD_Video_256x256x24 gpu_lcd_video_256x256x24_1: pin names not known; wires that end beside it: Reset_out, clock_1_out, gpu_lcd_video_256x256x24_1_p3, rom_1_data, gpu_lcd_video_256x256x24_1_p5
  // Probe on gpu_lcd_video_256x256x24_1_p5
  ROM #(.addrWidth(16), .dataWidth(2)) rom_2 (.addr(counter_1_q), .data(gpu_lcd_video_256x256x24_1_p3));

  // Notes on the sheet:
  //   contents of rom_1 (hex, n*v repeats v):
  //   compressed eJwt2OttXCEUReH/riIlXOC8KIfHof8Sgs2KLGUrUpbimetvIKV+f7/+lb8R441ShNHzjVqDMesb
  //   rS3Gsp+/IUpHNh01Opp0zOn4R8eDThQ6Mej0SqdPOqPRGYvOVDpz01lGZx062+nkRyeDzil0znid
  //   8tXFmK9zX4zXKWW9TqkqjP06pVkwDh1xOvrR0U7HCh0bdLzS8UknhE4sOl3p9KQzjM44dKbTWR+d
  //   1ensQmcPOtno5KRzhM5Zr1M/DUa+Ti22GOd17qPxOrV9g9Ffp0qhI4OONjo66ZjQsU3HlY4nnTA6
  //   cej0oDM+OqPTmZXOHHRWo7MmnS109qaTSieTznE657xO++J1WvmS0V+n1VoZ43Vaa69zf1Bep4nQ
  //   kU1HlY4mHXM6duh40IlCJzqdXun0QWc0OmPRmUJnbjrL6Kyks53OPnQy6JxC5/TXkftG/bwxX0dK
  //   G4z1OlIlGft1pFllJB1xOoo/ovgjhj9i+COOP+L4I4E/EvgjHX+k448M/JGBPzLxRxb+yMIf2fhz
  //   9aKT+COJP3LwRw7+6Ic/+uGPFvzRgj9a8Ucb/mjDHxX8UcEfVfxRxZ+LKB3DH3X8UccfDfzRwB/t
  //   +KMDf3Tgj0780Yk/uvBHF/7oxh/d+KOJP9dyOgd/9OCPffhjBX+s4I9V/LGKP9bwxxr+mOCPCf6Y
  //   4o8p/pjhjxn+3I8UOoE/FvhjHX+s448N/LGBPzbxxyb+2MIfW/hjG39s448l/tjBHzv4cz/ZXsc/
  //   /PGCP17wxyv+eMUfb/jjDX9c8McFf1zxxw1/3PDHHX/c8ccDf+4HLJ2OP97xxwf++MAfn/jjE398
  //   4Y9v/PGNP57444k/fvDHD/7Ehz/x4c/9nH+dKPgTFX+i4k80/AnBnxD8CcWfUPwJw58w/AnHn3D8
  //   icCfCPyJjj/3uEFn4E9M/ImJP7HwJxb+xMaf2PgTiT+R+BMHf+LgT//wpxf86QV/esWfe+p5nd7w
  //   pzf86YI/XfCnK/50xZ9u+NMNf7rjTw/86YE/veNP7/hzf6cz8OcevuhM/OkLf/rCn77xp2/86Yk/
  //   /eBPP/gzPvwZH/6Mgj+j4M+o+HP/Oa8zGv7cMyAdwZ8h+DMUf4bhzzD8GY4/w/FnBP6MwJ/R8Wd0
  //   /BkDf8bAn/uq0Jn4c4+idDb+jI0/I/FnJP6Mgz/j4M/88Gd++DML/syCP7Piz6z4Mxv+3DeHjuDP
  //   PRHTUfyZhj/T8Gc6/kzHnxn4MwN/Zsef2fFnDvyZE3/mxJ+58Oc+I3Q2/tyDOZ3En5n4Mw/+zIM/
  //   68Of9eHPKvizKv6sij+r4c9q+LMEf5bgz31U6Sj+3PsBHcOf5fizHH9W4M/q+LM6/qyBP2vgz5r4
  //   syb+rIU/a+HP2vhzf2LoJP7cawqdgz/7w5/94c8u+LML/uyKP7viz274sxv+bMGfLfizFX+24c/9
  //   waXj+HNvS3QCf3bgz+74szv+7IE/e+DPnvizJ/7shT9748/e+LMTf3biz/WDzsGfe2l7nfzwJwv+
  //   ZMGfrPiTFX+y4U8K/qTgTyr+pOJPGv6k4U86/lzG6AT+3LsjnY4/2fEnB/7kxJ+c+JMLf3LhT278
  //   yY0/mfiTiT958CcP/lxNFwN/7hX2dU7Fn1Px5zT8OQ1/juDPEfw5ij9H8ecY/hzDn+P4cxx/TuDP
  //   RZ1Ox597k6Yz8OdM/DkTf87Cn7Pw52z8ORt/TuLPSfw55/lTfm/wjOdPuVfxynj+3M/X58/vhf57
  //   f9KeP3dsOqJ0JOmo09FDx4KOFzre6USlE4NOb3T6ojOEzth0ptGZSWc5nXXo7KCThU52OqfSOc+f
  //   cr+fwXj+lFKeP3c8f0qpz587nj+ltOfP739v0JGgo4WOdjpW6dik442OLzqhdGLT6UanJ53hdOZH
  //   ZwadVeisQWdXOnvSyUYnF52jdM7z5349f+7X86fU8vy5j8jz547nT6nt+XPH86fccwcdmXRU6Oii
  //   Y0rHNh03On7ohNPpH53e6YxCZww6s9KZk84SOmvR2UpnJ500OnnonOdPad/z547nT2nl+XPH86e0
  //   +vy54/lTWnv+3LHoiNKRpKNGRw8dCzr+0fFOJwqdGHR6o9MnnSF0xqYzlc5MOsvorENnB5386GSn
  //   cyqd8/y5D/jz547nT5Hy/Lnj+VOkPn/ueP4Uac+fOw4dwR9R/BHFHzH8uWdSOo4/4vhz/zadwB/p
  //   +CMdf2Tgjwz8kYk/svBHFv7Ixh/Z+COJP5L4c4/GdA7+6Ic/95t4HS34owV/tOKPNvzRhj8q+KOC
  //   P6r4o4o/avijhj/q+HNP6HQCf7Tjz30t6Qz80YE/OvFHJ/7owh9d+KMbf3Tjjyb+aOKPHvyxD3/u
  //   ReF1rOCPFfy5b+lg4I81/LGGPyb4Y4I/pvhjij9m+GOOP+b4Y4E/Fvhz7yt0Ov7YwJ/7ZNGZ+GMT
  //   f2zhjy38sY0/lvhjiT928McO/viHP/7hjxf8udem1/GKP17x5z7gg4E/Lvjjij+u+OOGP274444/
  //   7vjjgT8e+OMdf7xn/fkP7XlVqw==
  //   GPU Data In
  //   contents of rom_2 (hex, n*v repeats v):
  //   702*3
  //   Don't forget to load the GPU's RAM
  //   with the file 'gpu4dram'.
  //   Right click on the GPU video screen.
  //   GPU Select
endmodule
